# Fritzing sketch scheme_arduino (saved by Fritzing 0.9.10b)
breadboards: 1

parts:
  Компонент1 = Arduino Nano (Rev3.0)
  ZS-042_RTC1 = ZS-042 RTC Module
  Компонент2 = Humidity Sensor - HIH-4030 Breakout
  LED1 = RGB LED (com. cathode, rgb) [package="5 mm [THT]"]
  S1 = Pushbutton [package="[THT]"]
  LCD1 = LCD screen  # not connected
  Компонент3 = Breakout Board for Electret Microphone
  Компонент4 = IFR520 MOS module [package=THT]

nets:
  N1: Компонент1.D1/TX, Компонент1.D2, S1.Pin_1, S1.Pin_2
  GND: Компонент1.GND, ZS-042_RTC1.GND, Компонент2.GND, LED1.common_cathode, S1.Pin_3, S1.Pin_4, Компонент3.GND, Компонент4.GND
  N2: Компонент1.D3, Компонент4.SIG
  N3: Компонент1.D4, Компонент2.OUT
  N4: Компонент1.D5, LED1.blue_anode
  N5: Компонент1.D6, LED1.green_anode
  N6: Компонент1.D7, LED1.red_anode
  N7: Компонент1.D8, Компонент3.AUD
  VCC: Компонент1.5V, ZS-042_RTC1.VCC, Компонент2.VCC, Компонент3.VCC, Компонент4.VCC
  N8: Компонент1.A5, ZS-042_RTC1.SCL
  N9: Компонент1.A4, ZS-042_RTC1.SDA

notes:
  MOSFET Транзистор
  RGB светодиод
  Датчик влажности
  Динамик
  Модуль часов реального времени
  Кнопка
  LCD дисплей
